# Fritzing sketch Main Circuit (saved by Fritzing 0.9.9b)

parts:
  Part2 = Arduino Mega 2560 (Rev3)  # not connected
  U1 = LM2596 step down module
  U2 = LM2596 step down module
  J1 = Power Jack [package=power_jack_smd]
  J2 = Camdenboss CTB0158-2 [part_number=CTB0158-2 package=THT]
  J3 = Camdenboss CTB0158-2 [part_number=CTB0158-2 package=THT]
  J4 = Camdenboss CTB0158-2 [part_number=CTB0158-2 package=THT]

nets:
  N1: U1.IN+, U2.IN+, J1.GNDBREAK, J4.pin1
  N2: U1.IN-, U1.OUT-, U2.IN-, U2.OUT-, J2.pin2, J3.pin2, J4.pin2
  N3: U1.OUT+, J2.pin1
  N4: U2.OUT+, J3.pin1

notes:
  5V Arduino
  5V Servos

custom parts:
  LM2596 step down module: LM2596 DC-DC step down power supply module 3 A.
